// Logisim project circuit.circ as structural Verilog: 3 circuits, main circuit main
module main (
);

  wire Clock, isRegA, isRegB, isRegC, isRegD, isRegE, isRegF;
  wire [15:0] RegisterA_q, undriven;

  InstructionDeterminer instructiondeterminer_1 ();  // open: ib1, ib2, ib3, ib4, ib5, ib6, ib7, ib8, ib9, ib10, ib11, ib12, ib13, ib14, ib15, ib16, isMOV
  RegisterDeterminer registerdeterminer_1 (
    .isRegA(isRegA), .isRegB(isRegB));  // open: ib1, ib2, ib3, ib4, ib5, ib6, ib7, ib8, ib9, ib10, ib11, ib12, ib13, ib14, ib15, ib16
  Clock clock_1 (.out(Clock));
  Register #(.width(16)) RegisterA (.D(undriven), .en(isRegA), .clk(Clock), .Q(RegisterA_q));  // open: clr
  Register #(.width(16)) RegisterB (.D(undriven), .en(isRegB), .clk(Clock), .Q(RegisterA_q));  // open: clr
  Register #(.width(16)) RegisterC (.D(undriven), .en(isRegC), .clk(Clock), .Q(RegisterA_q));  // open: clr
  Register #(.width(16)) RegisterD (.D(undriven), .en(isRegD), .clk(Clock), .Q(RegisterA_q));  // open: clr
  Register #(.width(16)) RegisterE (.D(undriven), .en(isRegE), .clk(Clock), .Q(RegisterA_q));  // open: clr
  Register #(.width(16)) RegisterF (.D(undriven), .en(isRegF), .clk(Clock), .Q(RegisterA_q));  // open: clr

  // Notes on the sheet:
  //   Data Load Bus
  //   Data Offload Bus
endmodule

module InstructionDeterminer (
  input  ib1,
  input  ib2,
  input  ib3,
  input  ib4,
  input  ib5,
  input  ib6,
  input  ib7,
  input  ib8,
  input  ib9,
  input  ib10,
  input  ib11,
  input  ib12,
  input  ib13,
  input  ib14,
  input  ib15,
  input  ib16,
  output isMOV
);

  wire and_1_out, and_2_out, and_3_out, and_4_out, and_5_out, and_6_out, and_7_out, and_8_out, and_9_out,
       and_10_out, and_11_out, and_12_out, and_13_out, and_14_out, not_1_out, not_2_out, not_3_out,
       not_4_out, not_5_out, not_6_out, not_7_out, not_8_out, not_9_out, not_10_out, not_11_out, not_12_out,
       not_13_out, not_14_out, not_15_out, not_16_out;

  not not_1 (not_1_out, ib1);
  not not_2 (not_2_out, ib2);
  not not_3 (not_3_out, ib3);
  not not_4 (not_4_out, ib4);
  not not_5 (not_5_out, ib5);
  not not_6 (not_6_out, ib6);
  not not_7 (not_7_out, ib7);
  not not_8 (not_8_out, ib8);
  not not_9 (not_9_out, ib9);
  not not_10 (not_10_out, ib10);
  not not_11 (not_11_out, ib11);
  not not_12 (not_12_out, ib12);
  not not_13 (not_13_out, ib13);
  not not_14 (not_14_out, ib14);
  not not_15 (not_15_out, ib15);
  not not_16 (not_16_out, ib16);
  and and_1 (and_1_out, not_1_out, not_2_out);
  and and_2 (and_2_out, not_3_out, not_4_out);
  and and_3 (and_3_out, not_5_out, not_6_out);
  and and_4 (and_4_out, not_7_out, not_8_out);
  and and_5 (and_5_out, not_9_out, not_10_out);
  and and_6 (and_6_out, not_11_out, not_12_out);
  and and_7 (and_7_out, not_13_out, not_14_out);
  and and_8 (and_8_out, not_15_out, not_16_out);
  and and_9 (and_9_out, and_1_out, and_2_out);
  and and_10 (and_10_out, and_3_out, and_4_out);
  and and_11 (and_11_out, and_5_out, and_6_out);
  and and_12 (and_12_out, and_7_out, and_8_out);
  and and_13 (and_13_out, and_9_out, and_10_out);
  and and_14 (and_14_out, and_11_out, and_12_out);
  and and_15 (isMOV, and_13_out, and_14_out);

  // Other names for the same wires on the sheet: cb1 = ib1; cb2 = ib2; cb3 = ib3; cb4 = ib4; cb5 = ib5; cb6 = ib6;
  //   cb7 = ib7; cb8 = ib8; cb9 = ib9; cb10 = ib10; cb11 = ib11; cb12 = ib12; cb13 = ib13; cb14 = ib14; cb15 = ib15;
  //   cb16 = ib16
endmodule

module RegisterDeterminer (
  input  ib1,
  input  ib2,
  input  ib3,
  input  ib4,
  input  ib5,
  input  ib6,
  input  ib7,
  input  ib8,
  input  ib9,
  input  ib10,
  input  ib11,
  input  ib12,
  input  ib13,
  input  ib14,
  input  ib15,
  input  ib16,
  output isRegA,
  output isRegB
);

  wire and_1_out, and_2_out, and_3_out, and_4_out, and_5_out, and_6_out, and_7_out, and_8_out, and_9_out,
       and_10_out, and_11_out, and_12_out, and_13_out, and_14_out, and_15_out, and_16_out, and_17_out,
       and_18_out, and_19_out, and_20_out, and_21_out, and_22_out, and_23_out, and_24_out, and_25_out,
       and_26_out, and_27_out, and_28_out, not_1_out, not_2_out, not_3_out, not_4_out, not_5_out, not_6_out,
       not_7_out, not_8_out, not_9_out, not_10_out, not_11_out, not_12_out, not_13_out, not_14_out,
       not_15_out, not_16_out, not_17_out, not_18_out, not_19_out, not_20_out, not_21_out, not_22_out,
       not_23_out, not_24_out, not_25_out, not_26_out, not_27_out, not_28_out, not_29_out, not_30_out,
       not_31_out;

  not not_1 (not_1_out, ib1);
  not not_2 (not_2_out, ib2);
  not not_3 (not_3_out, ib3);
  not not_4 (not_4_out, ib4);
  not not_5 (not_5_out, ib5);
  not not_6 (not_6_out, ib6);
  not not_7 (not_7_out, ib7);
  not not_8 (not_8_out, ib8);
  not not_9 (not_9_out, ib9);
  not not_10 (not_10_out, ib10);
  not not_11 (not_11_out, ib11);
  not not_12 (not_12_out, ib12);
  not not_13 (not_13_out, ib13);
  not not_14 (not_14_out, ib14);
  not not_15 (not_15_out, ib15);
  not not_16 (not_16_out, ib16);
  not not_17 (not_17_out, ib2);
  not not_18 (not_18_out, ib3);
  not not_19 (not_19_out, ib4);
  not not_20 (not_20_out, ib5);
  not not_21 (not_21_out, ib6);
  not not_22 (not_22_out, ib7);
  not not_23 (not_23_out, ib8);
  not not_24 (not_24_out, ib9);
  not not_25 (not_25_out, ib10);
  not not_26 (not_26_out, ib11);
  not not_27 (not_27_out, ib12);
  not not_28 (not_28_out, ib13);
  not not_29 (not_29_out, ib14);
  not not_30 (not_30_out, ib15);
  not not_31 (not_31_out, ib16);
  and and_1 (and_1_out, not_1_out, not_2_out);
  and and_2 (and_2_out, not_3_out, not_4_out);
  and and_3 (and_3_out, not_5_out, not_6_out);
  and and_4 (and_4_out, not_7_out, not_8_out);
  and and_5 (and_5_out, not_9_out, not_10_out);
  and and_6 (and_6_out, not_11_out, not_12_out);
  and and_7 (and_7_out, not_13_out, not_14_out);
  and and_8 (and_8_out, not_15_out, not_16_out);
  and and_9 (and_9_out, ib1, not_17_out);
  and and_10 (and_10_out, not_18_out, not_19_out);
  and and_11 (and_11_out, not_20_out, not_21_out);
  and and_12 (and_12_out, not_22_out, not_23_out);
  and and_13 (and_13_out, not_24_out, not_25_out);
  and and_14 (and_14_out, not_26_out, not_27_out);
  and and_15 (and_15_out, not_28_out, not_29_out);
  and and_16 (and_16_out, not_30_out, not_31_out);
  and and_17 (and_17_out, and_1_out, and_2_out);
  and and_18 (and_18_out, and_3_out, and_4_out);
  and and_19 (and_19_out, and_5_out, and_6_out);
  and and_20 (and_20_out, and_7_out, and_8_out);
  and and_21 (and_21_out, and_9_out, and_10_out);
  and and_22 (and_22_out, and_11_out, and_12_out);
  and and_23 (and_23_out, and_13_out, and_14_out);
  and and_24 (and_24_out, and_15_out, and_16_out);
  and and_25 (and_25_out, and_21_out, and_22_out);
  and and_26 (and_26_out, and_23_out, and_24_out);
  and and_27 (and_27_out, and_17_out, and_18_out);
  and and_28 (and_28_out, and_19_out, and_20_out);
  and and_29 (isRegA, and_27_out, and_28_out);
  and and_30 (isRegB, and_25_out, and_26_out);

  // Other names for the same wires on the sheet: cb1 = ib1; cb2 = ib2; cb3 = ib3; cb4 = ib4; cb5 = ib5; cb6 = ib6;
  //   cb7 = ib7; cb8 = ib8; cb9 = ib9; cb10 = ib10; cb11 = ib11; cb12 = ib12; cb13 = ib13; cb14 = ib14; cb15 = ib15;
  //   cb16 = ib16
endmodule
